# Fritzing sketch bata_midi_arduino (saved by Fritzing 0.8.3b)
breadboards: 1

parts:
  R1 = Resistor [tolerance=±5% resistance=10k package=THT]
  Parte1 = Arduino Uno (Rev3)
  DIN1 = DIN-5 jack (MIDI) [package=THT]
  LED1 = LED - 5mm [color="Red (633nm)" package="5 mm [THT]"]
  J2 = Piezo Speaker
  R4 = Resistor [tolerance=±5% resistance=47k package=THT]
  R5 = Resistor [tolerance=±5% resistance=220k package=THT]

nets:
  N1: R1.Pin_0, LED1.anode
  N2: R1.Pin_1, Parte1.D8
  N3: Parte1.A1, J2.pin1, R4.Pin_0
  N4: Parte1.GND, J2.pin2, R4.Pin_1
  N5: Parte1.D3_PWM, DIN1.5
  N6: Parte1.5V, LED1.cathode, R5.Pin_0
  N7: DIN1.4, R5.Pin_1
