# Fritzing sketch bata_midi_deploy (saved by Fritzing 0.8.3b)
breadboards: 1

parts:
  C1 = Electrolytic Capacitor [capacitance=1µF package="100 mil [THT, electrolytic]"]
  C2 = Electrolytic Capacitor [capacitance=1µF package="100 mil [THT, electrolytic]"]  # not connected
  U1 = Voltage Regulator - 5V [package="TO220 [THT]"]
  LED1 = LED - 5mm [color="Red (633nm)" package="5 mm [THT]"]
  R1 = Resistor [tolerance=±5% resistance=220 package=THT]
  U2 = atmega328 [package=dip]
  R2 = Resistor [tolerance=±5% resistance=220 package=THT]
  C3 = Ceramic Capacitor [capacitance=100nF package="100 mil [THT, multilayer]"]
  C4 = Ceramic Capacitor [capacitance=100nF package="100 mil [THT, multilayer]"]
  XTAL1 = Crystal [frequency="16 Mhz" package=THT]
  S1 = Pushbutton [package="[THT]"]
  R29 = Resistor [tolerance=±5% resistance=47k package=THT]
  DIN3 = DIN-5 jack (MIDI) [package=THT]
  R31 = Resistor [tolerance=±5% resistance=220 package=THT]
  R32 = Resistor [tolerance=±5% resistance=220k package=THT]
  J14 = Piezo Speaker
  J15 = Piezo Speaker
  R33 = Resistor [tolerance=±5% resistance=47k package=THT]
  J16 = Piezo Speaker
  R34 = Resistor [tolerance=±5% resistance=47k package=THT]
  J17 = Piezo Speaker
  R35 = Resistor [tolerance=±5% resistance=47k package=THT]

nets:
  N1: C1.-, U1.output_voltage, LED1.cathode, R1.Pin_0, U2.VCC, U2.AVCC, U2.AREF, R2.Pin_0, S1.Pin_3, S1.Pin_4, R32.Pin_0
  GND: C1.+, U1.GND, U2.GND, C3.0, C4.0, R29.Pin_1, DIN3.2, J14.pin1, J15.pin1, R33.Pin_1, R34.Pin_1, J17.pin1, R35.Pin_1
  N2: LED1.anode, R1.Pin_1
  N3: U2.RESET, R2.Pin_1, S1.Pin_1, S1.Pin_2
  N4: U2.D3_(PWM), R31.Pin_0
  N5: U2.XLAT1, C3.1, XTAL1.pin_0
  N6: U2.XLAT2, C4.1, XTAL1.pin_1
  N7: U2.A0, R29.Pin_0, J14.pin2
  N8: U2.A1, J15.pin2, R33.Pin_0
  N9: U2.A2, J16.pin2, R34.Pin_0
  N10: U2.A3, J17.pin2, R35.Pin_0
  N11: DIN3.5, R31.Pin_1
  N12: DIN3.4, R32.Pin_1
