# Fritzing sketch bata_midi_pcb (saved by Fritzing 0.8.5b)
circuit board: 8.41732cm x 4.95554cm
breadboards: 1

parts:
  U2 = Voltage Regulator - 5V [package="TO220 [THT]"]
  C1 = Electrolytic Capacitor [capacitance=10µF package="100 mil [THT, electrolytic]"]
  C2 = Electrolytic Capacitor [capacitance=10µF package="100 mil [THT, electrolytic]"]
  VCC1 = Battery block 9V
  S2 = SWITCH-MOMENTARY-2 [package=tactile-switch-1101ne]
  LED1 = LED - 5mm [color="Red (633nm)" package="5 mm [THT]"]
  U3 = atmega328 [package=dip]
  XTAL1 = Crystal [frequency="16 Mhz" package=THT]
  C3 = Capacitor [package=cap-pth-small2]
  C4 = Capacitor [package=cap-pth-small2]
  S3 = Pushbutton [package="[THT]"]
  R2 = Resistor [tolerance=±5% resistance=220 package=THT]
  J1 = female pin header, 3 pins [form="♀ (female)"]
  R1 = Resistor [tolerance=±5% resistance=220 package=THT]
  R3 = Resistor [tolerance=±5% resistance=220 package=THT]
  J2 = shrouded pin header, 8 pins [form="♂ (shrouded male)"]

nets:
  N1: U2.input_voltage, C1.+, VCC1.+
  N2: U2.GND, C1.-, C2.-, VCC1.-, LED1.cathode, U3.AREF
  N3: U2.output_voltage, C2.+, S2.2
  N4: S2.1, U3.GND, U3.XLAT1, R2.Pin_1, R1.Pin_1, R3.Pin_0, J2.pin8
  N5: LED1.anode, R1.Pin_0
  N6: U3.D0_(RX), J2.pin1
  N7: U3.D1_(TX), J2.pin2
  N8: U3.D2, J2.pin3
  N9: U3.D3_(PWM), J2.pin4
  N10: U3.D4, J2.pin5
  N11: U3.VCC, U3.A5, C3.2, C4.2, S3.Pin_1, S3.Pin_2, R2.Pin_0, J1.pin3, J2.pin7
  N12: U3.D13, XTAL1.pin_1, C3.1
  N13: U3.AVCC, XTAL1.pin_0, C4.1
  N14: U3.A3, J1.pin1
  N15: J1.pin2, R3.Pin_1

notes:
  midi slot
  piezos slot
